# Fritzing sketch Motor (saved by Fritzing 0.9.3b)

parts:
  L298N1 = L298N DC motor driver
  Raspberry_Pi_1 = Raspberry Pi 4 [part_number=RPI-4-b]
  M1 = DC Motor  # not connected
  VCC1 = 4 x AAA Battery Mount  # not connected

nets:
  N1: L298N1.ENA, Raspberry_Pi_1.GPIO25
  N2: L298N1.IN1, Raspberry_Pi_1.GPIO23
  N3: L298N1.IN2, Raspberry_Pi_1.GPIO24

custom parts:
  L298N DC motor driver: 2x DC motor driver with 78M05 positive voltage regulator (7..35 V) L298N: max 46 V, 2 A Set 5 V Enable jumper to enable 5 V regultor (needed for the L298N) and +5 V output at screw terminal or supply external +5 V at screw terminal Set ENA and/or ENB to +5 V to enable motor permanently or supply ENA and/or ENB with PWM signal IN1 and IN2 set rotation directory for motor A (OUT1/OUT2) IN2 and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
  Raspberry Pi 4: The RPi4, a faster version of the awesome Raspberry Pi 2 B ARM Board with 40 pin gpio. Ready for special Raspberry Pi B+ and RPi2 Hat (Hardware attached (on) top)
