# Fritzing sketch Servo_Motor (saved by Fritzing 0.9.3b)

parts:
  Raspberry_Pi_1 = Raspberry Pi 4 [part_number=RPI-4-b]
  J1 = Basic Servo

nets:
  N1: Raspberry_Pi_1.GPIO25, J1.pulse
  GND: Raspberry_Pi_1.GND, J1.gnd
  5V: Raspberry_Pi_1.5V, J1.vcc

custom parts:
  Raspberry Pi 4: The RPi4, a faster version of the awesome Raspberry Pi 2 B ARM Board with 40 pin gpio. Ready for special Raspberry Pi B+ and RPi2 Hat (Hardware attached (on) top)
