# Fritzing sketch Accelerometre (saved by Fritzing 0.9.3b)

parts:
  Composant1 = InvenSense MPU6050
  Raspberry_Pi_1 = Raspberry Pi 4 [part_number=RPI-4-b]

nets:
  VCC: Composant1.VCC, Raspberry_Pi_1.5V
  GND: Composant1.GND, Raspberry_Pi_1.GND
  N1: Composant1.SCL, Raspberry_Pi_1.GPIO3
  N2: Composant1.SDA, Raspberry_Pi_1.GPIO2

custom parts:
  Raspberry Pi 4: The RPi4, a faster version of the awesome Raspberry Pi 2 B ARM Board with 40 pin gpio. Ready for special Raspberry Pi B+ and RPi2 Hat (Hardware attached (on) top)
