# Fritzing sketch Photoresistor (saved by Fritzing 0.9.3b)

parts:
  Raspberry_Pi_1 = Raspberry Pi 4 [part_number=RPI-4-b]
  LED1 = LED - 5mm [color="Red (633nm)" package="5 mm [THT]"]
  R1 = PHOTOCELL [package=photocell-kit]
  R2 = Resistor [tolerance=±5% resistance=220 package=THT]
  C1 = Capacitor Polarized [package=cpol-radial-10uf-25v]  # not connected

nets:
  N1: Raspberry_Pi_1.3v3, R1.P$2
  N2: Raspberry_Pi_1.GPIO24, R2.Pin_1
  N3: Raspberry_Pi_1.GND, LED1.cathode

custom parts:
  Raspberry Pi 4: The RPi4, a faster version of the awesome Raspberry Pi 2 B ARM Board with 40 pin gpio. Ready for special Raspberry Pi B+ and RPi2 Hat (Hardware attached (on) top)
